# Fritzing sketch lokcontroller (saved by Fritzing 1.0.3b)
breadboards: 1

parts:
  U1 = L9110 H-bridge module [part_number="L9110 H-bridge"]
  LED1 = RGB LED (com. cathode, rbg) [color="Red (633nm)" current=30mA package="5 mm [THT]"]
  VCC1 = Battery block 9V [internal_resistance=0.1Ω]
  M1 = DC Motor [voltage_(max)=6V voltage_(min)=3V]
  Mod1 = Amica NodeMCU DEVKIT 1.0

nets:
  N1: U1.B-IA, Mod1.pin_14
  N2: U1.B-IB, Mod1.pin_13
  N3: U1.GND, LED1.common_cathode, VCC1.-, Mod1.pin2, Mod1.pin_9, Mod1.pin_25, Mod1.pin_29
  N4: U1.VCC, VCC1.+, Mod1.pin_30
  N5: U1.MOTOR_B-A, M1.pin_2
  N6: U1.MOTOR_B-B, M1.pin_1
  N7: LED1.red_anode, Mod1.pin8
  N8: LED1.blue_anode, Mod1.pin7
  N9: LED1.green_anode, Mod1.pin6
  N10: Mod1.pin1, Mod1.pin_10, Mod1.pin_26
